# Fritzing sketch Horloge Bodet (saved by Fritzing 0.9.1b)
circuit board: 8.46667cm x 5.64444cm
breadboards: 1

parts:
  IC2 = H-Bridge [package=THT]
  C1 = Ceramic Capacitor [capacitance=100nF package="100 mil [THT, multilayer]"]
  C2 = Ceramic Capacitor [capacitance=100nF package="100 mil [THT, multilayer]"]
  R1 = Resistor [tolerance=±5% resistance=470 package=THT]
  LED1 = LED - 5mm [color="Red (633nm)" package="5 mm [THT]"]
  C3 = Electrolytic Capacitor [capacitance=0.1mF package="100 mil [THT, electrolytic]"]
  U1 = AVR 10-pin ICSP Header [package=avr_icsp]
  R2 = Resistor [tolerance=±5% resistance=22k package=THT]
  R3 = Resistor [tolerance=±5% resistance=47 package=THT]
  S2 = SPDT Slide Switch [package=ayz0202]
  S1 = SPST Switch [package=switch-spdt-smd]
  JP5 = Header 6 [package=molex-1x6-ra]
  JP6 = Header 2 [package=jst-2-pth-kit]
  IC1 = atmega328 [package=dip]
  J2 = Power Jack [package=power_jack_slot]

nets (from the schematic view):
  N1: IC2.1_2EN, IC2.VCC2, IC2.VCC1, C1.1, C2.0, C3.+, U1.2, R2.Pin_1, S1.P, JP5.1, IC1.VCC
  N2: IC2.1A, S2.5, IC1.D10_(PWM)
  N3: IC2.1Y, JP6.2
  GND1: IC2.GND1, IC2.GND2, IC2.3_4EN, IC2.3A, IC2.GND3, IC2.GND4, IC2.4A, C2.1, R1.Pin_0, C3.-, U1.4, U1.6, U1.8, U1.10, S2.3, J2.GNDBREAK
  N4: IC2.2Y, R3.Pin_0
  N5: IC2.2A, IC1.D9_(PWM)
  N6: C1.0, JP5.5, IC1.GND
  N7: R1.Pin_1, LED1.cathode
  N8: LED1.anode, S2.6
  N9: U1.1, IC1.D11_(PWM)
  N10: U1.5, R2.Pin_0, IC1.RESET
  N11: U1.7, IC1.D13
  N12: U1.9, IC1.D12
  N13: R3.Pin_1, JP6.1
  N14: S2.2, IC1.D3_(PWM)
  N15: S1.S, J2.PWR
  N16: JP5.2, IC1.A5
  N17: JP5.3, IC1.D2
  N18: JP5.6, IC1.A4

notes:
  Marche / Arrêt
  Avance Rapide
  Moteur PàP Horloge Bodet
  Port ICSP
  DS3231 Breakout board
  DS3231 Breakout Board
